# Fritzing sketch TempControlLayout (saved by Fritzing 0.9.1b)

parts:
  Bauteil1 = Arduino Uno (Rev3)
  HC = DHT11 Humitidy and Temperature Sensor
  W = DHT11 Humitidy and Temperature Sensor
  Tiny_RTC1 = Tiny RTC
  U1 = ESP8266 WiFi Module [part_number=ESP8266]

nets:
  N1: Bauteil1.A4/SDA, Tiny_RTC1.SDA
  N2: Bauteil1.A5/SCL, Tiny_RTC1.SCL
  GND: Bauteil1.GND, HC.GND, W.GND, Tiny_RTC1.GND, U1.GND
  N3: Bauteil1.D2, W.DATA
  N4: Bauteil1.D4, HC.DATA
  VDD: Bauteil1.5V, HC.VDD, W.VDD, Tiny_RTC1.VCC

custom parts:
  DHT11 Humitidy and Temperature Sensor: DHT11 Humidity and Temperature Sensor
  Tiny RTC: Tiny RTC I2C module DS1370Z RTC and AT24C32 EEPROM
  ESP8266 WiFi Module: Generic WiFi Module based on the ESP8266 with onboard PCB antenna and UART communications
